# Fritzing sketch hardware (saved by Fritzing 0.5.2b)
breadboards: 1

parts:
  Arduino1 = Arduino Nano v2.3
  J1 = female pin header, 15 pins [form="♂ (male)"]
  R1 = Resistor [resistance=10k package=THT]
  R2 = Resistor [resistance=10k package=THT]
  R3 = Resistor [resistance=10k package=THT]
  R4 = Resistor [resistance=10k package=THT]
  R5 = Resistor [resistance=100k package=THT]
  R6 = Resistor [resistance=100k package=THT]
  R7 = Resistor [resistance=100k package=THT]
  R8 = Resistor [resistance=100k package=THT]

nets:
  N1: Arduino1.GND, J1.pin4, J1.pin5, J1.pin12, R5.Pin_1, R6.Pin_1, R7.Pin_1, R8.Pin_1
  N2: Arduino1.D2, J1.pin2, R2.Pin_1
  N3: Arduino1.D3, J1.pin7, R1.Pin_1
  N4: Arduino1.D5, J1.pin14, R3.Pin_1
  N5: Arduino1.D6, J1.pin10, R4.Pin_1
  N6: Arduino1.A4, J1.pin13, R8.Pin_0
  N7: Arduino1.A3, J1.pin11, R7.Pin_0
  N8: Arduino1.A1, J1.pin6, R6.Pin_0
  N9: Arduino1.A0, J1.pin3, R5.Pin_0
  N10: Arduino1.+5V, J1.pin1, J1.pin9, R1.Pin_0, R2.Pin_0, R3.Pin_0, R4.Pin_0
